// Logisim project bonkpu.circ as structural Verilog: 1 circuit, main circuit main
module main (
);

  wire button_1_out, not_1_out;
  wire [2:0] FLAGS_p2;
  wire [3:0] MICROSTEP_q;
  wire [7:0] OP_REG_q;
  wire [23:0] microcode_c_data;

  Button button_1 (.out(button_1_out));
  Counter #(.max('hf), .width(4)) MICROSTEP (
    .load(microcode_c_data[0]), .clk(not_1_out), .D(4'b0000), .Q(MICROSTEP_q));  // open: clr, up, count, carry
  not not_1 (not_1_out, button_1_out);
  // DipSwitch #(.number(3)) FLAGS: pin names not known; wires that end beside it: not_1_out, FLAGS_p2[0], FLAGS_p2[1], FLAGS_p2[2]
  Register OP_REG (.D({8{1'b0}}), .en(microcode_c_data[18]), .clk(button_1_out), .Q(OP_REG_q));  // open: clr
  ROM #(.addrWidth(15)) microcode_a (.addr({FLAGS_p2, OP_REG_q, MICROSTEP_q}), .data(microcode_c_data[23:16]));
  ROM #(.addrWidth(15)) microcode_b (.addr({FLAGS_p2, OP_REG_q, MICROSTEP_q}), .data(microcode_c_data[15:8]));
  LedBar #(.matrixcols(24)) ledbar_1 (
    .led0(microcode_c_data[23]), .led1(microcode_c_data[22]), .led2(microcode_c_data[21]),
    .led3(microcode_c_data[20]), .led4(microcode_c_data[19]), .led5(microcode_c_data[18]),
    .led6(microcode_c_data[17]), .led7(microcode_c_data[16]), .led8(microcode_c_data[15]),
    .led9(microcode_c_data[14]), .led10(microcode_c_data[13]), .led11(microcode_c_data[12]),
    .led12(microcode_c_data[11]), .led13(microcode_c_data[10]), .led14(microcode_c_data[9]),
    .led15(microcode_c_data[8]), .led16(microcode_c_data[7]), .led17(microcode_c_data[6]),
    .led18(microcode_c_data[5]), .led19(microcode_c_data[4]), .led20(microcode_c_data[3]),
    .led21(microcode_c_data[2]), .led22(microcode_c_data[1]), .led23(microcode_c_data[0]));
  ROM #(.addrWidth(15)) microcode_c (.addr({FLAGS_p2, OP_REG_q, MICROSTEP_q}), .data(microcode_c_data[7:0]));

  // Notes on the sheet:
  //   contents of microcode_a (hex, n*v repeats v):
  //   40 20 c 13*0 40 20 c 0 40 20 9 9*0 40 20 c 0 40 20 8 1 8*0 40 20 c 0 40 20 8 40 20 8 6*0 40 20 c
  //   13*0 40 20 c 0 40 20 8 40 20 8 6*0 40 20 c 13*0 40 20 c 0 40 20 8 40 20 8 6*0 40 20 c 13*0 40 20 c 0
  //   40 20 8 40 20 8 6*0 40 20 c 13*0 40 20 c 13*0 40 20 c 0 80 11*0 40 20 c 13*0 40 20 c 13*0 40 20 c
  //   13*0 40 20 c 13*0 40 20 c 13*0 40 20 c 13*0 40 20 c 13*0 40 20 c 13*0 40 20 c 13*0 40 20 c 13*0 40
  //   20 c 13*0 40 20 c 13*0 40 20 c 13*0 40 20 c 13*0 40 20 c 13*0 40 20 c 13*0 40 20 c 13*0 40 20 c 13*0
  //   40 20 c 13*0 40 20 c 13*0 40 20 c 13*0 40 20 c 13*0 40 20 c 13*0 40 20 c 13*0 40 20 c 13*0 40 20 c
  //   13*0 40 20 c 13*0 40 20 c 13*0 40 20 c 13*0 40 20 c 13*0 40 20 c 13*0 40 20 c 13*0 40 20 c 13*0 40
  //   20 c 13*0 40 20 c 13*0 40 20 c 13*0 40 20 c 13*0 40 20 c 13*0 40 20 c 13*0 40 20 c 13*0 40 20 c 13*0
  //   40 20 c 13*0 40 20 c 13*0 40 20 c 13*0 40 20 c 13*0 40 20 c 13*0 40 20 c 13*0 40 20 c 13*0 40 20 c
  //   13*0 40 20 c 13*0 40 20 c 13*0 40 20 c 13*0 40 20 c 13*0 40 20 c 13*0 40 20 c 13*0 40 20 c 13*0 40
  //   20 c 13*0 40 20 c 13*0 40 20 c 13*0 40 20 c 13*0 40 20 c 13*0 40 20 c 13*0 40 20 c 13*0 40 20 c 13*0
  //   40 20 c 13*0 40 20 c 13*0 40 20 c 13*0 40 20 c 13*0 40 20 c 13*0 40 20 c 13*0 40 20 c 13*0 40 20 c
  //   13*0 40 20 c 13*0 40 20 c 13*0 40 20 c 13*0 40 20 c 13*0 40 20 c 13*0 40 20 c 13*0 40 20 c 13*0 40
  //   20 c 13*0 40 20 c 13*0 40 20 c 13*0 40 20 c 13*0 40 20 c 13*0 40 20 c 13*0 40 20 c 13*0 40 20 c 13*0
  //   40 20 c 13*0 40 20 c 13*0 40 20 c 13*0 40 20 c 13*0 40 20 c 13*0 40 20 c 13*0 40 20 c 13*0 40 20 c
  //   13*0 40 20 c 13*0 40 20 c 13*0 40 20 c 13*0 40 20 c 13*0 40 20 c 13*0 40 20 c 13*0 40 20 c 13*0 40
  //   20 c 13*0 40 20 c 13*0 40 20 c 13*0 40 20 c 13*0 40 20 c 13*0 40 20 c 13*0 40 20 c 13*0 40 20 c 13*0
  //   40 20 c 13*0 40 20 c 13*0 40 20 c 13*0 40 20 c 13*0 40 20 c 13*0 40 20 c 13*0 40 20 c 13*0 40 20 c
  //   13*0 40 20 c 13*0 40 20 c 13*0 40 20 c 13*0 40 20 c 13*0 40 20 c 13*0 40 20 c 13*0 40 20 c 13*0 40
  //   20 c 13*0 40 20 c 13*0 40 20 c 13*0 40 20 c 13*0 40 20 c 13*0 40 20 c 13*0 40 20 c 13*0 40 20 c 13*0
  //   40 20 c 13*0 40 20 c 13*0 40 20 c 13*0 40 20 c 13*0 40 20 c 13*0 40 20 c 13*0 40 20 c 13*0 40 20 c
  //   13*0 40 20 c 13*0 40 20 c 13*0 40 20 c 13*0 40 20 c 13*0 40 20 c 13*0 40 20 c 13*0 40 20 c 13*0 40
  //   20 c 13*0 40 20 c 13*0 40 20 c 13*0 40 20 c 13*0 40 20 c 13*0 40 20 c 13*0 40 20 c 13*0 40 20 c 13*0
  //   40 20 c 13*0 40 20 c 13*0 40 20 c 13*0 40 20 c 13*0 40 20 c 13*0 40 20 c 13*0 40 20 c 13*0 40 20 c
  //   13*0 40 20 c 13*0 40 20 c 13*0 40 20 c 13*0 40 20 c 13*0 40 20 c 13*0 40 20 c 13*0 40 20 c 13*0 40
  //   20 c 13*0 40 20 c 13*0 40 20 c 13*0 40 20 c 13*0 40 20 c 13*0 40 20 c 13*0 40 20 c 13*0 40 20 c 13*0
  //   40 20 c 13*0 40 20 c 13*0 40 20 c 13*0 40 20 c 13*0 40 20 c 13*0 40 20 c 13*0 40 20 c 13*0 40 20 c
  //   13*0 40 20 c 13*0 40 20 c 13*0 40 20 c 13*0 40 20 c 13*0 40 20 c 13*0 40 20 c 13*0 40 20 c 13*0 40
  //   20 c 13*0 40 20 c 13*0 40 20 c 13*0 40 20 c 13*0 40 20 c 13*0 40 20 c 13*0 40 20 c 13*0 40 20 c 13*0
  //   40 20 c 13*0 40 20 c 13*0 40 20 c 13*0 40 20 c 13*0 40 20 c 13*0 40 20 c 13*0 40 20 c 13*0 40 20 c
  //   13*0 40 20 c 13*0 40 20 c 13*0 40 20 c 13*0 40 20 c 13*0 40 20 c 13*0 40 20 c 13*0 40 20 c 13*0 40
  //   20 c 13*0 40 20 c 13*0 40 20 c 13*0 40 20 c 13*0 40 20 c 13*0 40 20 c 13*0 40 20 c 13*0 40 20 c 13*0
  //   40 20 c 13*0 40 20 c 13*0 40 20 c 13*0 40 20 c 13*0 40 20 c 13*0 40 20 c 13*0 40 20 c 13*0 40 20 c
  //   13*0 40 20 c 13*0 40 20 c 13*0 40 20 c 13*0 40 20 c 13*0 40 20 c 13*0 40 20 c 13*0 40 20 c 13*0 40
  //   20 c 13*0 40 20 c 13*0 40 20 c 13*0 40 20 c 13*0 40 20 c 0 40 20 9 9*0 40 20 c 0 40 20 8 1 8*0 40 20
  //   c 0 40 20 8 40 20 8 6*0 40 20 c 0 40 20 8 40 20 8 6*0 40 20 c 13*0 40 20 c 13*0 40 20 c 0 40 20 8 40
  //   20 8 6*0 40 20 c 13*0 40 20 c 0 40 20 8 40 20 8 6*0 40 20 c 13*0 40 20 c 13*0 40 20 c 0 80 11*0 40
  //   20 c 13*0 40 20 c 13*0 40 20 c 13*0 40 20 c 13*0 40 20 c 13*0 40 20 c 13*0 40 20 c 13*0 40 20 c 13*0
  //   40 20 c 13*0 40 20 c 13*0 40 20 c 13*0 40 20 c 13*0 40 20 c 13*0 40 20 c 13*0 40 20 c 13*0 40 20 c
  //   13*0 40 20 c 13*0 40 20 c 13*0 40 20 c 13*0 40 20 c 13*0 40 20 c 13*0 40 20 c 13*0 40 20 c 13*0 40
  //   20 c 13*0 40 20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
  //   contents of microcode_b (hex, n*v repeats v):
  //   0 0 2 2 14*0 2 2 1 0 2 11*0 2 2 1 0 42 14 10*0 2 2 1 0 42 1 0 2 20 7*0 4*2 12*0 2 2 1 0 42 1 0 2 20
  //   7*0 4*2 12*0 2 2 1 0 42 1 0 2 20 7*0 4*2 12*0 2 2 1 0 42 1 0 2 20 7*0 4*2 12*0 4*2 12*0 2 2 14*0 2 2
  //   14*0 2 2 14*0 2 2 14*0 2 2 14*0 2 2 14*0 2 2 14*0 2 2 14*0 2 2 14*0 2 2 14*0 2 2 14*0 2 2 14*0 2 2
  //   14*0 2 2 14*0 2 2 14*0 2 2 14*0 2 2 14*0 2 2 14*0 2 2 14*0 2 2 14*0 2 2 14*0 2 2 14*0 2 2 14*0 2 2
  //   14*0 2 2 14*0 2 2 14*0 2 2 14*0 2 2 14*0 2 2 14*0 2 2 14*0 2 2 14*0 2 2 14*0 2 2 14*0 2 2 14*0 2 2
  //   14*0 2 2 14*0 2 2 14*0 2 2 14*0 2 2 14*0 2 2 14*0 2 2 14*0 2 2 14*0 2 2 14*0 2 2 14*0 2 2 14*0 2 2
  //   14*0 2 2 14*0 2 2 14*0 2 2 14*0 2 2 14*0 2 2 14*0 2 2 14*0 2 2 14*0 2 2 14*0 2 2 14*0 2 2 14*0 2 2
  //   14*0 2 2 14*0 2 2 14*0 2 2 14*0 2 2 14*0 2 2 14*0 2 2 14*0 2 2 14*0 2 2 14*0 2 2 14*0 2 2 14*0 2 2
  //   14*0 2 2 14*0 2 2 14*0 2 2 14*0 2 2 14*0 2 2 14*0 2 2 14*0 2 2 14*0 2 2 14*0 2 2 14*0 2 2 14*0 2 2
  //   14*0 2 2 14*0 2 2 14*0 2 2 14*0 2 2 14*0 2 2 14*0 2 2 14*0 2 2 14*0 2 2 14*0 2 2 14*0 2 2 14*0 2 2
  //   14*0 2 2 14*0 2 2 14*0 2 2 14*0 2 2 14*0 2 2 14*0 2 2 14*0 2 2 14*0 2 2 14*0 2 2 14*0 2 2 14*0 2 2
  //   14*0 2 2 14*0 2 2 14*0 2 2 14*0 2 2 14*0 2 2 14*0 2 2 14*0 2 2 14*0 2 2 14*0 2 2 14*0 2 2 14*0 2 2
  //   14*0 2 2 14*0 2 2 14*0 2 2 14*0 2 2 14*0 2 2 14*0 2 2 14*0 2 2 14*0 2 2 14*0 2 2 14*0 2 2 14*0 2 2
  //   14*0 2 2 14*0 2 2 14*0 2 2 14*0 2 2 14*0 2 2 14*0 2 2 14*0 2 2 14*0 2 2 14*0 2 2 14*0 2 2 14*0 2 2
  //   14*0 2 2 14*0 2 2 14*0 2 2 14*0 2 2 14*0 2 2 14*0 2 2 14*0 2 2 14*0 2 2 14*0 2 2 14*0 2 2 14*0 2 2
  //   14*0 2 2 14*0 2 2 14*0 2 2 14*0 2 2 14*0 2 2 14*0 2 2 14*0 2 2 14*0 2 2 14*0 2 2 14*0 2 2 14*0 2 2
  //   14*0 2 2 14*0 2 2 14*0 2 2 14*0 2 2 14*0 2 2 14*0 2 2 14*0 2 2 14*0 2 2 14*0 2 2 14*0 2 2 14*0 2 2
  //   14*0 2 2 14*0 2 2 14*0 2 2 14*0 2 2 14*0 2 2 14*0 2 2 14*0 2 2 14*0 2 2 14*0 2 2 14*0 2 2 14*0 2 2
  //   14*0 2 2 14*0 2 2 14*0 2 2 14*0 2 2 14*0 2 2 14*0 2 2 14*0 2 2 14*0 2 2 14*0 2 2 14*0 2 2 14*0 2 2
  //   14*0 2 2 14*0 2 2 14*0 2 2 14*0 2 2 14*0 2 2 14*0 2 2 14*0 2 2 14*0 2 2 14*0 2 2 14*0 2 2 14*0 2 2
  //   14*0 2 2 14*0 2 2 14*0 2 2 14*0 2 2 14*0 2 2 14*0 2 2 14*0 2 2 14*0 2 2 14*0 2 2 14*0 2 2 14*0 2 2
  //   14*0 2 2 14*0 2 2 14*0 2 2 14*0 2 2 14*0 2 2 14*0 2 2 14*0 2 2 14*0 2 2 14*0 2 2 14*0 2 2 14*0 2 2
  //   14*0 2 2 14*0 2 2 14*0 2 2 14*0 2 2 14*0 2 2 14*0 2 2 14*0 2 2 14*0 2 2 14*0 2 2 14*0 2 2 14*0 2 2
  //   14*0 2 2 14*0 2 2 14*0 2 2 14*0 2 2 14*0 2 2 14*0 2 2 14*0 2 2 14*0 2 2 14*0 2 2 14*0 2 2 14*0 2 2
  //   14*0 2 2 14*0 2 2 1 0 2 11*0 2 2 1 0 42 14 10*0 2 2 1 0 42 1 0 2 20 7*0 2 2 1 0 42 1 0 2 20 7*0 4*2
  //   12*0 4*2 12*0 2 2 1 0 42 1 0 2 20 7*0 4*2 12*0 2 2 1 0 42 1 0 2 20 7*0 4*2 12*0 4*2 12*0 2 2 14*0 2
  //   2 14*0 2 2 14*0 2 2 14*0 2 2 14*0 2 2 14*0 2 2 14*0 2 2 14*0 2 2 14*0 2 2 14*0 2 2 14*0 2 2 14*0 2 2
  //   14*0 2 2 14*0 2 2 14*0 2 2 14*0 2 2 14*0 2 2 14*0 2 2 14*0 2 2 14*0 2 2 14*0 2 2 14*0 2 2 14*0 2 2
  //   14*0 2 2 14*0 2 2 14*0 2 2 14*0 2 2 14*0 2 2 14*0 2 2 14*0 2 2 14*0 2 2 14*0 2 2 14*0 2 2 14*0 2 2
  //   14*0 2 2 14*0 2 2 14*0 2 2 14*0 2 2 14*0 2 2 14*0 2 2 14*0 2 2 14*0 2 2 14*0 2 2 14*0 2 2 14*0 2 2
  //   14*0 2 2 14*0 2 2 14*0 2 2 14*0 2 2 14*0 2 2 14*0 2 2 14*0 2 2 14*0 2 2 14*0 2 2 14*0 2 2 14*0 2 2
  //   14*0 2 2 14*0 2 2 14*0 2 2 14*0 2 2 14*0 2 2 14*0 2 2 14*0 2 2 14*0 2 2 14*0 2 2 14*0 2 2 14*0 2 2
  //   14*0 2 2 14*0 2 2 14*0 2 2 14*0 2 2 14*0 2 2 14*0 2 2 14*0 2 2 14*0 2 2 14*0 2 2 14*0 2 2 14*0 2 2
  //   14*0 2 2 14*0 2 2 14*0 2 2 14*0 2 2 14*0 2 2 14*0 2 2 14*0 2 2 14*0 2 2 14*0 2 2 14*0 2 2 14*0 2 2
  //   14*0 2 2 14*0 2 2 14*0 2 2 14*0 2 2 14*0 2 2 14*0 2 2 14*0 2 2 14*0 2 2 14*0 2 2 14*0 2 2 14*0 2 2
  //   14*0 2 2 14*0 2 2 14*0 2 2 14*0 2 2 14*0 2 2 14*0 2 2 14*0 2 2 14*0 2 2 14*0 2 2 14*0 2 2 14*0 2 2
  //   14*0 2 2 14*0 2 2 14*0 2 2 14*0 2 2 14*0 2 2 14*0 2 2 14*0 2 2 14*0 2 2 14*0 2 2 14*0 2 2 14*0 2 2
  //   14*0 2 2 14*0 2 2 14*0 2 2 14*0 2 2 14*0 2 2 14*0 2 2 14*0 2 2 14*0 2 2 14*0 2 2 14*0 2 2 14*0 2 2
  //   14*0 2 2 14*0 2 2 14*0 2 2 14*0 2 2 14*0 2 2 14*0 2 2 14*0 2 2 14*0 2 2 14*0 2 2 14*0 2 2 14*0 2 2
  //   14*0 2 2 14*0 2 2 14*0 2 2 14*0 2 2 14*0 2 2 14*0 2 2 14*0 2 2 14*0 2 2 14*0 2 2 14*0 2 2 14*0 2 2
  //   14*0 2 2 14*0 2 2 14*0 2 2 14*0 2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
  //   contents of microcode_c (hex, n*v repeats v):
  //   40 20 0 1 12*0 40 20 0 0 0 80 1 9*0 40 20 0 0 0 80 0 1 8*0 40 20 0 0 0 80 0 0 80 40 21 5*0 40 20 0 0
  //   0 1 10*0 40 20 0 0 0 80 0 0 80 40 21 5*0 40 20 0 0 0 1 10*0 40 20 0 0 0 80 0 0 80 40 21 5*0 40 20 0
  //   0 0 1 10*0 40 20 0 0 0 80 0 0 80 40 21 5*0 40 20 0 0 0 1 10*0 40 20 0 0 0 1 10*0 40 20 0 0 1 11*0 40
  //   20 0 1 12*0 40 20 0 1 12*0 40 20 0 1 12*0 40 20 0 1 12*0 40 20 0 1 12*0 40 20 0 1 12*0 40 20 0 1
  //   12*0 40 20 0 1 12*0 40 20 0 1 12*0 40 20 0 1 12*0 40 20 0 1 12*0 40 20 0 1 12*0 40 20 0 1 12*0 40 20
  //   0 1 12*0 40 20 0 1 12*0 40 20 0 1 12*0 40 20 0 1 12*0 40 20 0 1 12*0 40 20 0 1 12*0 40 20 0 1 12*0
  //   40 20 0 1 12*0 40 20 0 1 12*0 40 20 0 1 12*0 40 20 0 1 12*0 40 20 0 1 12*0 40 20 0 1 12*0 40 20 0 1
  //   12*0 40 20 0 1 12*0 40 20 0 1 12*0 40 20 0 1 12*0 40 20 0 1 12*0 40 20 0 1 12*0 40 20 0 1 12*0 40 20
  //   0 1 12*0 40 20 0 1 12*0 40 20 0 1 12*0 40 20 0 1 12*0 40 20 0 1 12*0 40 20 0 1 12*0 40 20 0 1 12*0
  //   40 20 0 1 12*0 40 20 0 1 12*0 40 20 0 1 12*0 40 20 0 1 12*0 40 20 0 1 12*0 40 20 0 1 12*0 40 20 0 1
  //   12*0 40 20 0 1 12*0 40 20 0 1 12*0 40 20 0 1 12*0 40 20 0 1 12*0 40 20 0 1 12*0 40 20 0 1 12*0 40 20
  //   0 1 12*0 40 20 0 1 12*0 40 20 0 1 12*0 40 20 0 1 12*0 40 20 0 1 12*0 40 20 0 1 12*0 40 20 0 1 12*0
  //   40 20 0 1 12*0 40 20 0 1 12*0 40 20 0 1 12*0 40 20 0 1 12*0 40 20 0 1 12*0 40 20 0 1 12*0 40 20 0 1
  //   12*0 40 20 0 1 12*0 40 20 0 1 12*0 40 20 0 1 12*0 40 20 0 1 12*0 40 20 0 1 12*0 40 20 0 1 12*0 40 20
  //   0 1 12*0 40 20 0 1 12*0 40 20 0 1 12*0 40 20 0 1 12*0 40 20 0 1 12*0 40 20 0 1 12*0 40 20 0 1 12*0
  //   40 20 0 1 12*0 40 20 0 1 12*0 40 20 0 1 12*0 40 20 0 1 12*0 40 20 0 1 12*0 40 20 0 1 12*0 40 20 0 1
  //   12*0 40 20 0 1 12*0 40 20 0 1 12*0 40 20 0 1 12*0 40 20 0 1 12*0 40 20 0 1 12*0 40 20 0 1 12*0 40 20
  //   0 1 12*0 40 20 0 1 12*0 40 20 0 1 12*0 40 20 0 1 12*0 40 20 0 1 12*0 40 20 0 1 12*0 40 20 0 1 12*0
  //   40 20 0 1 12*0 40 20 0 1 12*0 40 20 0 1 12*0 40 20 0 1 12*0 40 20 0 1 12*0 40 20 0 1 12*0 40 20 0 1
  //   12*0 40 20 0 1 12*0 40 20 0 1 12*0 40 20 0 1 12*0 40 20 0 1 12*0 40 20 0 1 12*0 40 20 0 1 12*0 40 20
  //   0 1 12*0 40 20 0 1 12*0 40 20 0 1 12*0 40 20 0 1 12*0 40 20 0 1 12*0 40 20 0 1 12*0 40 20 0 1 12*0
  //   40 20 0 1 12*0 40 20 0 1 12*0 40 20 0 1 12*0 40 20 0 1 12*0 40 20 0 1 12*0 40 20 0 1 12*0 40 20 0 1
  //   12*0 40 20 0 1 12*0 40 20 0 1 12*0 40 20 0 1 12*0 40 20 0 1 12*0 40 20 0 1 12*0 40 20 0 1 12*0 40 20
  //   0 1 12*0 40 20 0 1 12*0 40 20 0 1 12*0 40 20 0 1 12*0 40 20 0 1 12*0 40 20 0 1 12*0 40 20 0 1 12*0
  //   40 20 0 1 12*0 40 20 0 1 12*0 40 20 0 1 12*0 40 20 0 1 12*0 40 20 0 1 12*0 40 20 0 1 12*0 40 20 0 1
  //   12*0 40 20 0 1 12*0 40 20 0 1 12*0 40 20 0 1 12*0 40 20 0 1 12*0 40 20 0 1 12*0 40 20 0 1 12*0 40 20
  //   0 1 12*0 40 20 0 1 12*0 40 20 0 1 12*0 40 20 0 1 12*0 40 20 0 1 12*0 40 20 0 1 12*0 40 20 0 1 12*0
  //   40 20 0 1 12*0 40 20 0 1 12*0 40 20 0 1 12*0 40 20 0 1 12*0 40 20 0 1 12*0 40 20 0 1 12*0 40 20 0 1
  //   12*0 40 20 0 1 12*0 40 20 0 1 12*0 40 20 0 1 12*0 40 20 0 1 12*0 40 20 0 1 12*0 40 20 0 1 12*0 40 20
  //   0 1 12*0 40 20 0 1 12*0 40 20 0 1 12*0 40 20 0 1 12*0 40 20 0 1 12*0 40 20 0 1 12*0 40 20 0 1 12*0
  //   40 20 0 1 12*0 40 20 0 1 12*0 40 20 0 1 12*0 40 20 0 1 12*0 40 20 0 1 12*0 40 20 0 1 12*0 40 20 0 1
  //   12*0 40 20 0 1 12*0 40 20 0 1 12*0 40 20 0 1 12*0 40 20 0 1 12*0 40 20 0 1 12*0 40 20 0 1 12*0 40 20
  //   0 1 12*0 40 20 0 1 12*0 40 20 0 1 12*0 40 20 0 1 12*0 40 20 0 1 12*0 40 20 0 1 12*0 40 20 0 1 12*0
  //   40 20 0 1 12*0 40 20 0 1 12*0 40 20 0 1 12*0 40 20 0 1 12*0 40 20 0 1 12*0 40 20 0 1 12*0 40 20 0 1
  //   12*0 40 20 0 1 12*0 40 20 0 1 12*0 40 20 0 1 12*0 40 20 0 1 12*0 40 20 0 1 12*0 40 20 0 1 12*0 40 20
  //   0 1 12*0 40 20 0 1 12*0 40 20 0 1 12*0 40 20 0 1 12*0 40 20 0 1 12*0 40 20 0 1 12*0 40 20 0 1 12*0
  //   40 20 0 1 12*0 40 20 0 1 12*0 40 20 0 1 12*0 40 20 0 1 12*0 40 20 0 1 12*0 40 20 0 1 12*0 40 20 0 1
  //   12*0 40 20 0 1 12*0 40 20 0 1 12*0 40 20 0 1 12*0 40 20 0 1 12*0 40 20 0 1 12*0 40 20 0 1 12*0 40 20
  //   0 1 12*0 40 20 0 1 12*0 40 20 0 1 12*0 40 20 0 1 12*0 40 20 0 1 12*0 40 20 0 1 12*0 40 20 0 1 12*0
  //   40 20 0 1 12*0 40 20 0 1 12*0 40 20 0 1 12*0 40 20 0 1 12*0 40 20 0 0 0 80 1 9*0 40 20 0 0 0 80 0 1
  //   8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
endmodule
